# Fritzing sketch racing_car (saved by Fritzing 0.9.4)
breadboards: 1

parts:
  Raspberry_Pi_1 = Raspberry Pi 3 [part_number=RPI-3-V1.2]
  R1 = Resistor [tolerance=±5% resistance=2k package=THT]
  R2 = Resistor [tolerance=±5% resistance=2k package=THT]
  R3 = Photocell (LDR) [package=THT]
  R4 = Photocell (LDR) [package=THT]
  U1 = 74HC595 [package="DIP16 [THT]"]
  LED1 = LED - 5mm [color="Red (633nm)" package="5 mm [THT]"]
  LED2 = LED - 5mm [color="Red (633nm)" package="5 mm [THT]"]
  LED3 = LED - 5mm [color="Red (633nm)" package="5 mm [THT]"]
  LED4 = LED - 5mm [color="Green (555nm)" package="5 mm [THT]"]
  R5 = Resistor [tolerance=±5% resistance=220 package=THT]
  R6 = Resistor [tolerance=±5% resistance=220 package=THT]
  R7 = Resistor [tolerance=±5% resistance=220 package=THT]
  R8 = Resistor [tolerance=±5% resistance=220 package=THT]
  J1 = Piezo Speaker
  S1 = Pushbutton [package="[THT]"]
  R9 = Resistor [tolerance=±5% resistance=220 package=THT]
  S2 = Pushbutton [package="[THT]"]

nets:
  N1: Raspberry_Pi_1.3v3, R3.pin_1, R4.pin_1, R9.Pin_1
  N2: Raspberry_Pi_1.GND, R1.Pin_1, R2.Pin_1, U1.OE, LED1.cathode, LED2.cathode, LED3.cathode, LED4.cathode, J1.pin1
  N3: Raspberry_Pi_1.GPIO17, R2.Pin_0, R4.pin_0
  N4: Raspberry_Pi_1.GPIO27, U1.SH_CP
  N5: Raspberry_Pi_1.GPIO22, U1.DS
  N6: Raspberry_Pi_1.GPIO9, S2.Pin_3, S2.Pin_4
  N7: Raspberry_Pi_1.GPIO25, S1.Pin_3, S1.Pin_4
  N8: Raspberry_Pi_1.GPIO24, J1.pin2
  N9: Raspberry_Pi_1.GPIO23, U1.ST_CP
  N10: Raspberry_Pi_1.GPIO18, R1.Pin_0, R3.pin_0
  5V: Raspberry_Pi_1.5V, U1.MR, U1.VCC
  N11: U1.Q1, R6.Pin_0
  N12: U1.Q2, R7.Pin_0
  N13: U1.Q3, R8.Pin_0
  N14: U1.Q0, R5.Pin_0
  N15: LED1.anode, R5.Pin_1
  N16: LED2.anode, R6.Pin_1
  N17: LED3.anode, R7.Pin_1
  N18: LED4.anode, R8.Pin_1
  N19: S1.Pin_1, S1.Pin_2, R9.Pin_0, S2.Pin_2
