# Fritzing sketch racing_car_hat (saved by Fritzing 0.9.4)
perfboards: 2

parts:
  J2 = Raspberry Pi Header 40pin [form="♂ (male)" package=THT]
  JP2 = Header 6 [package=1x06_smd_straight_alt]
  R5 = Resistor [tolerance=±5% resistance=2k package=THT]
  R6 = Resistor [tolerance=±5% resistance=2k package=THT]
  R7 = Resistor [tolerance=±5% resistance=2k package=THT]
  J3 = Piezo Speaker
  U2 = 74HC595 [package="DIP16 [THT]"]
  R8 = Resistor [tolerance=±5% resistance=220 package=THT]
  R9 = Resistor [tolerance=±5% resistance=220 package=THT]
  R10 = Resistor [tolerance=±5% resistance=220 package=THT]
  R11 = Resistor [tolerance=±5% resistance=220 package=THT]
  LED2 = LED - 5mm [color="Red (633nm)" package="5 mm [THT]"]
  LED3 = LED - 5mm [color="Red (633nm)" package="5 mm [THT]"]
  LED4 = LED - 5mm [color="Red (633nm)" package="5 mm [THT]"]
  LED5 = LED - 5mm [color="Green (555nm)" package="5 mm [THT]"]
  J5 = Raspberry Pi Header 40pin [form="♂ (male)" package=THT]
  JP3 = Header 6 [package=1x06_smd_straight_alt]
  R12 = Resistor [tolerance=±5% resistance=2k package=THT]
  R13 = Resistor [tolerance=±5% resistance=2k package=THT]
  R14 = Resistor [tolerance=±5% resistance=2k package=THT]
  U3 = 74HC595 [package="DIP16 [THT]"]
  R15 = Resistor [tolerance=±5% resistance=220 package=THT]
  R16 = Resistor [tolerance=±5% resistance=220 package=THT]
  R17 = Resistor [tolerance=±5% resistance=220 package=THT]
  LED6 = LED - 5mm [color="Green (555nm)" package="5 mm [THT]"]  # not connected
  R18 = Resistor [tolerance=±5% resistance=220 package=THT]  # not connected
  LED7 = LED - 5mm [color="Red (633nm)" package="5 mm [THT]"]  # not connected

nets:
  3V3: J2.3v3, J2.3V3, JP2.1, R7.Pin_0
  N1: J2.GIPO4, U2.DS
  N2: J2.GND, R5.Pin_1, R6.Pin_1, J3.pin1, U2.OE, LED2.cathode, LED3.cathode, LED4.cathode, LED5.cathode
  N3: J2.GIPO17, U2.ST_CP
  N4: J2.GIPO27, U2.SH_CP
  N5: J2.GIPO5, JP2.2, R6.Pin_0
  N6: J2.GIPO6, JP2.3, R5.Pin_0
  N7: J2.GIPO13, JP2.5
  N8: J2.GIPO19, JP2.6
  5V: J2.5V, U2.VCC
  N9: JP2.4, R7.Pin_1
  N10: U2.Q1, R9.Pin_1
  N11: U2.Q2, R10.Pin_1
  N12: U2.Q3, R11.Pin_1
  N13: R8.Pin_0, LED2.anode
  N14: R9.Pin_0, LED3.anode
  N15: R10.Pin_0, LED4.anode
  N16: R11.Pin_0, LED5.anode
  3V3_2: J5.3v3, J5.3V3, JP3.1, R14.Pin_1
  N17: J5.GIPO4, U3.DS
  N18: J5.GND, R12.Pin_1, R13.Pin_1, U3.OE
  N19: J5.GIPO17, U3.ST_CP
  N20: J5.GIPO27, U3.SH_CP
  N21: J5.GIPO5, JP3.2
  N22: J5.GIPO6, JP3.3
  N23: J5.GIPO13, JP3.5
  N24: J5.GIPO19, JP3.6
  5V_2: J5.5V, U3.VCC
  N25: U3.Q1, R17.Pin_1
  N26: U3.Q2, R16.Pin_1
  N27: U3.Q3, R15.Pin_1

custom parts:
  Raspberry Pi Header 40pin: Raspberry Pi 40 pin header - for creating your own shields.
